// Logisim project SomadorComSubtratorSequencial.circ as structural Verilog: 1 circuit, main circuit main
module main (
  input  Op,
  input  A3,
  input  A2,
  input  A1,
  input  A0,
  input  B3,
  input  B2,
  input  B1,
  input  B0
);

  wire decodificador_1_a_2, decodificador_1_b_2, decodificador_1_c_2, decodificador_1_d_2, decodificador_1_e,
       decodificador_1_f, decodificador_1_g, main_1_s, main_2_bcout, main_2_s, main_3_bcout, main_3_s,
       main_4_bcout, main_4_s;

  SomadorComSubtrator_main main_1 (.X(Op), .A(A3), .B(B3), .Cin(main_2_bcout), .S(main_1_s));  // open: BCout
  SomadorComSubtrator_main main_2 (.X(Op), .A(A2), .B(B2), .Cin(main_3_bcout), .S(main_2_s), .BCout(main_2_bcout));
  SomadorComSubtrator_main main_3 (.X(Op), .A(A1), .B(B1), .Cin(main_4_bcout), .S(main_3_s), .BCout(main_3_bcout));
  SomadorComSubtrator_main main_4 (.X(Op), .A(A0), .B(B0), .Cin(1'b0), .S(main_4_s), .BCout(main_4_bcout));
  Decodificador decodificador_1 (
    .A(main_1_s), .B(main_2_s), .C(main_3_s), .D(main_4_s), .a_2(decodificador_1_a_2),
    .b_2(decodificador_1_b_2), .c_2(decodificador_1_c_2), .d_2(decodificador_1_d_2), .e(decodificador_1_e),
    .f(decodificador_1_f), .g(decodificador_1_g));
  _7_Segment_Display u_7_segment_display_1 (
    .g(decodificador_1_g), .f(decodificador_1_f), .a(decodificador_1_a_2), .b(decodificador_1_b_2),
    .e(decodificador_1_e), .d(decodificador_1_d_2), .c(decodificador_1_c_2));  // open: dp
endmodule
