// Logisim project SomadorSequencial.circ as structural Verilog: 1 circuit, main circuit main
module main (
  input  A3,
  input  A2,
  input  A1,
  input  A0,
  input  B3,
  input  B2,
  input  B1,
  input  B0,
  output S1,
  output S2,
  output S1_2,
  output S0
);

  wire main_1_p1, main_2_p1;

  // Somador_Completo_main main_1: pin names not known; wires that end beside it: main_1_p1, B3, A3, S1
  // Somador_Completo_main main_2: pin names not known; wires that end beside it: main_2_p1, B2, main_1_p1, A2, S2
  // Somador_Completo_main main_3: pin names not known; wires that end beside it: S0, B1, main_2_p1, A1, S1_2
  // Somador_Completo_main main_4: pin names not known; wires that end beside it: 1'b0, B0, A0
endmodule
