// Logisim project SubtratorDecode.circ as structural Verilog: 1 circuit, main circuit main
module main (
  input  in_1,
  input  in_2,
  input  in_3,
  input  in_4,
  input  in_5,
  input  in_6,
  input  in_7,
  input  in_8
);

  wire decodificador_1_a_2, decodificador_1_b_2, decodificador_1_c_2, decodificador_1_d_2, decodificador_1_e,
       decodificador_1_f, decodificador_1_g, main_1_p1, main_1_p4, main_2_p1, main_2_p5, main_3_p1,
       main_3_p5, main_4_p5;

  // SubtratorCompleto_main main_1: pin names not known; wires that end beside it: main_1_p1, in_5, in_1, main_1_p4
  // SubtratorCompleto_main main_2: pin names not known; wires that end beside it: main_2_p1, in_6, main_1_p1, in_2, main_2_p5
  // SubtratorCompleto_main main_3: pin names not known; wires that end beside it: main_3_p1, in_7, main_2_p1, in_3, main_3_p5
  // SubtratorCompleto_main main_4: pin names not known; wires that end beside it: 1'b0, in_8, main_3_p1, in_4, main_4_p5
  Decodificador decodificador_1 (
    .A(main_1_p4), .B(main_2_p5), .C(main_3_p5), .D(main_4_p5), .a_2(decodificador_1_a_2),
    .b_2(decodificador_1_b_2), .c_2(decodificador_1_c_2), .d_2(decodificador_1_d_2), .e(decodificador_1_e),
    .f(decodificador_1_f), .g(decodificador_1_g));
  _7_Segment_Display u_7_segment_display_1 (
    .g(decodificador_1_g), .f(decodificador_1_f), .a(decodificador_1_a_2), .b(decodificador_1_b_2),
    .e(decodificador_1_e), .d(decodificador_1_d_2), .c(decodificador_1_c_2));  // open: dp
endmodule
